# Fritzing sketch SmartPlantMidTermrecover (saved by Fritzing 0.9.4)
breadboards: 1

parts:
  Argon1 = Particle Argon
  Relay1 = Relay - 6 pins [package="DIP (Dual Inline) [THT]"]
  SENS1 = SoilWatch 10
  OLED_I2C1 = OLED 128x64 I2C Monochrome Display
  Part1 = BME280 Breakout
  Q1 = PNP-Transistor [package="TO92 [THT]"]
  R1 = Resistor [tolerance=±5% resistance=220 package="0603 [SMD]"]
  R2 = 2.2k Ω Resistor [package="0603 [SMD]"]
  M1 = DC Motor
  Grove1 = Grove Dust Sensor
  U1 = AQ_Sensor [package=mq-3]

nets:
  VCC: Argon1.3.3V, Relay1.VCC, SENS1.VCC, OLED_I2C1.VDD, Part1.3.3V, Grove1.VCC, U1.Vcc
  GND: Argon1.GND, Relay1.GND, SENS1.GND, OLED_I2C1.GND, Part1.GND, Q1.B, R2.Pin_0, M1.pin_2, Grove1.GND, U1.GND
  N1: Argon1.A0, SENS1.OUT
  N2: Argon1.MI, Q1.C, R2.Pin_1
  N3: Argon1.SDA, OLED_I2C1.SDA, Part1.SDI/SDA
  N4: Argon1.SCL, OLED_I2C1.SCK, Part1.SCK/SCL
  N5: Argon1.D5, Grove1.SIG
  N6: Argon1.VUSB, Relay1.ON, R1.Pin_0
  N7: Relay1.IN, Q1.E, R1.Pin_1
  N8: Relay1.COM, M1.pin_1

custom parts:
  Particle Argon: The Argon is a powerful Wi-Fi enabled development board that can act as either a standalone Wi-Fi endpoint or Wi-Fi enabled gateway for Particle Mesh networks. It is based on the Nordic nRF52840 and has built-in battery charging circuitry so it’s easy to connect a Li-Po and deploy your local network in minutes. The Argon is great for connecting existing projects to the Particle Device Cloud or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
  Relay - 6 pins: A DIP stand-in part for whatever IC you want. With 6 pins on a 900mil dual inline package (DIP) footprint.
  SoilWatch 10: SoilWatch 10 - Capacitive soil moisture sensor
  2.2k Ω Resistor: A generic resistor (0.25W)
  Grove Dust Sensor: PPD42 Grove Dust Sensor
  AQ_Sensor: MQ-3 alcohol gas sensor . FP not tested. SEN-08880.
